// Logisim project cpu.circ as structural Verilog: 7 circuits, main circuit d-latch
module d_latch (
  input  enabler,
  input  \input ,
  output Q,
  output Q_prime
);

  wire and_1_out, and_2_out, not_1_out;

  not not_1 (not_1_out, \input );
  and and_1 (and_1_out, not_1_out, enabler);
  and and_2 (and_2_out, enabler, \input );
  nor nor_1 (Q, and_1_out, Q_prime);
  nor nor_2 (Q_prime, Q, and_2_out);
endmodule

module d_flip_flop (
  input  d,
  input  e,
  output q,
  output q_prime
);

  wire d_latch_1_q_prime, not_1_out, not_2_out;

  d_latch d_latch_1 (.Q_prime(d_latch_1_q_prime), .\input (d), .enabler(not_1_out));  // open: Q
  not not_1 (not_1_out, e);
  not not_2 (not_2_out, not_1_out);
  d_latch d_latch_2 (.Q(q), .Q_prime(q_prime), .\input (d_latch_1_q_prime), .enabler(not_2_out));
endmodule

module full_adder_1_bit (
  input  input_1_1_bit,
  input  input_2_1_bit,
  input  carry_in,
  output carry_out,
  output result
);

  wire and_1_out, and_2_out, and_3_out;

  and and_1 (and_1_out, input_1_1_bit, input_2_1_bit);
  and and_2 (and_2_out, input_2_1_bit, carry_in);
  and and_3 (and_3_out, input_1_1_bit, carry_in);
  ExactlyOne xor_1 (.out(result), .in0(input_1_1_bit), .in1(input_2_1_bit), .in2(carry_in));
  or or_1 (carry_out, and_1_out, and_2_out, and_3_out);
endmodule

module full_adder_4_bit (
  input  [3:0] input1_4_bit,
  input  [3:0] input2_4_bit,
  input  carry_in,
  output carry_out,
  output [3:0] \output 
);

  wire full_adder_1_bit_2_carry_out, full_adder_1_bit_3_carry_out, full_adder_1_bit_4_carry_out;

  full_adder_1_bit full_adder_1_bit_1 (
    .input_1_1_bit(input1_4_bit[3]), .input_2_1_bit(input2_4_bit[3]),
    .carry_in(full_adder_1_bit_2_carry_out), .carry_out(carry_out), .result(\output [3]));
  full_adder_1_bit full_adder_1_bit_2 (
    .input_1_1_bit(input1_4_bit[2]), .input_2_1_bit(input2_4_bit[2]),
    .carry_in(full_adder_1_bit_3_carry_out), .carry_out(full_adder_1_bit_2_carry_out), .result(\output [2]));
  full_adder_1_bit full_adder_1_bit_3 (
    .input_1_1_bit(input1_4_bit[1]), .input_2_1_bit(input2_4_bit[1]),
    .carry_in(full_adder_1_bit_4_carry_out), .carry_out(full_adder_1_bit_3_carry_out), .result(\output [1]));
  full_adder_1_bit full_adder_1_bit_4 (
    .input_1_1_bit(input1_4_bit[0]), .input_2_1_bit(input2_4_bit[0]), .carry_in(carry_in),
    .carry_out(full_adder_1_bit_4_carry_out), .result(\output [0]));
endmodule

module full_adder_16_bit (
  input  [15:0] input_1_16_bit,
  input  [15:0] input__16_bit,
  input  carry_in,
  output carry_out,
  output [15:0] \output 
);

  wire full_adder_4_bit_2_carry_out, full_adder_4_bit_3_carry_out, full_adder_4_bit_4_carry_out;

  full_adder_4_bit full_adder_4_bit_1 (
    .input1_4_bit(input_1_16_bit[15:12]), .input2_4_bit(input__16_bit[15:12]),
    .carry_in(full_adder_4_bit_2_carry_out), .carry_out(carry_out), .\output (\output [15:12]));
  full_adder_4_bit full_adder_4_bit_2 (
    .input1_4_bit(input_1_16_bit[11:8]), .input2_4_bit(input__16_bit[11:8]),
    .carry_in(full_adder_4_bit_3_carry_out), .carry_out(full_adder_4_bit_2_carry_out),
    .\output (\output [11:8]));
  full_adder_4_bit full_adder_4_bit_3 (
    .input1_4_bit(input_1_16_bit[7:4]), .input2_4_bit(input__16_bit[7:4]),
    .carry_in(full_adder_4_bit_4_carry_out), .carry_out(full_adder_4_bit_3_carry_out),
    .\output (\output [7:4]));
  full_adder_4_bit full_adder_4_bit_4 (
    .input1_4_bit(input_1_16_bit[3:0]), .input2_4_bit(input__16_bit[3:0]), .carry_in(carry_in),
    .carry_out(full_adder_4_bit_4_carry_out), .\output (\output [3:0]));
endmodule

module full_adder_18_bit (
  input  [17:0] in_1,
  input  [17:0] in_2,
  input  carry_in,
  output carry_out,
  output [17:0] out_5
);

  wire full_adder_1_bit_1_carry_out, full_adder_1_bit_2_carry_out;

  full_adder_16_bit full_adder_16_bit_1 (
    .input_1_16_bit(in_1[17:2]), .input__16_bit(in_2[17:2]), .carry_in(full_adder_1_bit_1_carry_out),
    .carry_out(carry_out), .\output (out_5[17:2]));
  full_adder_1_bit full_adder_1_bit_1 (
    .input_1_1_bit(in_1[1]), .input_2_1_bit(in_2[1]), .carry_in(full_adder_1_bit_2_carry_out),
    .carry_out(full_adder_1_bit_1_carry_out), .result(out_5[1]));
  full_adder_1_bit full_adder_1_bit_2 (
    .input_1_1_bit(in_1[0]), .input_2_1_bit(in_2[0]), .carry_in(carry_in),
    .carry_out(full_adder_1_bit_2_carry_out), .result(out_5[0]));
endmodule

module register (
  input  [17:0] loadingBit,
  input  enabler_bit,
  output [17:0] outputBit
);

  d_latch d_latch_1 (.Q(outputBit[0]), .\input (loadingBit[0]), .enabler(enabler_bit));  // open: Q_prime
  d_latch d_latch_2 (.Q(outputBit[1]), .\input (loadingBit[1]), .enabler(enabler_bit));  // open: Q_prime
  d_latch d_latch_3 (.Q(outputBit[2]), .\input (loadingBit[2]), .enabler(enabler_bit));  // open: Q_prime
  d_latch d_latch_4 (.Q(outputBit[3]), .\input (loadingBit[3]), .enabler(enabler_bit));  // open: Q_prime
  d_latch d_latch_5 (.Q(outputBit[4]), .\input (loadingBit[4]), .enabler(enabler_bit));  // open: Q_prime
  d_latch d_latch_6 (.Q(outputBit[5]), .\input (loadingBit[5]), .enabler(enabler_bit));  // open: Q_prime
  d_latch d_latch_7 (.Q(outputBit[6]), .\input (loadingBit[6]), .enabler(enabler_bit));  // open: Q_prime
  d_latch d_latch_8 (.Q(outputBit[7]), .\input (loadingBit[7]), .enabler(enabler_bit));  // open: Q_prime
  d_latch d_latch_9 (.Q(outputBit[8]), .\input (loadingBit[8]), .enabler(enabler_bit));  // open: Q_prime
  d_latch d_latch_10 (.Q(outputBit[9]), .\input (loadingBit[9]), .enabler(enabler_bit));  // open: Q_prime
  d_latch d_latch_11 (.Q(outputBit[10]), .\input (loadingBit[10]), .enabler(enabler_bit));  // open: Q_prime
  d_latch d_latch_12 (.Q(outputBit[11]), .\input (loadingBit[11]), .enabler(enabler_bit));  // open: Q_prime
  d_latch d_latch_13 (.Q(outputBit[12]), .\input (loadingBit[12]), .enabler(enabler_bit));  // open: Q_prime
  d_latch d_latch_14 (.Q(outputBit[13]), .\input (loadingBit[13]), .enabler(enabler_bit));  // open: Q_prime
  d_latch d_latch_15 (.Q(outputBit[14]), .\input (loadingBit[14]), .enabler(enabler_bit));  // open: Q_prime
  d_latch d_latch_16 (.Q(outputBit[15]), .\input (loadingBit[15]), .enabler(enabler_bit));  // open: Q_prime
  d_latch d_latch_17 (.Q(outputBit[16]), .\input (loadingBit[16]), .enabler(enabler_bit));  // open: Q_prime
  d_latch d_latch_18 (.Q(outputBit[17]), .\input (loadingBit[17]), .enabler(enabler_bit));  // open: Q_prime
endmodule
