// Logisim project d latch.circ as structural Verilog: 1 circuit, main circuit d-latch
module d_latch (
  input  D,
  input  enable,
  output Q,
  output Q_prime
);

  wire nand_1_out, nand_2_out, nand_3_out, nand_4_out;

  nand nand_1 (nand_1_out, D, enable);
  nand nand_2 (nand_2_out, nand_1_out, enable);
  nand nand_3 (nand_3_out, nand_1_out, nand_4_out);
  nand nand_4 (nand_4_out, nand_3_out, nand_2_out);
endmodule
